// Logisim project ex2.circ as structural Verilog: 1 circuit, main circuit compute_BrUn
module compute_BrUn (
  input  [31:0] INSTRUCTION,
  output BrUn
);

  Multiplexer #(.select(2)) multiplexer_1 (
    .in0(1'b0), .in1(1'b0), .in2(1'b0), .in3(1'b1), .out(BrUn), .sel(INSTRUCTION[14:13]));

  // Other names for the same wires on the sheet: opcode[6:0] = INSTRUCTION[6:0]; funct3[2:0] = INSTRUCTION[14:12]
endmodule
